// Logisim project 2-to-1_MUX.circ as structural Verilog: 1 circuit, main circuit main
module main (
  input  Input_0,
  input  Input_1,
  input  A,
  output Z
);

  Multiplexer #(.enable("false")) multiplexer_1 (.in0(Input_0), .in1(Input_1), .out(Z), .sel(A));

  // Notes on the sheet:
  //   A=0 => Z=Input-0
  //   A=1 => Z=Input-1
  //   Z=A'Input-0+AInput-1
endmodule
