// Logisim project 3-to-8_Decoder_AND.circ as structural Verilog: 1 circuit, main circuit main
module main (
  input  C,
  input  B,
  input  A,
  output O0,
  output O1,
  output O2,
  output O3,
  output O4,
  output O5,
  output O6,
  output O7
);

  wire not_1_out, not_2_out, not_3_out;

  not not_1 (not_1_out, C);
  not not_2 (not_2_out, B);
  not not_3 (not_3_out, A);
  and and_1 (O0, not_3_out, not_2_out, not_1_out);
  and and_2 (O1, not_3_out, not_2_out, C);
  and and_3 (O2, not_3_out, B, not_1_out);
  and and_4 (O3, not_3_out, B, C);
  and and_5 (O4, A, not_2_out, not_1_out);
  and and_6 (O5, A, not_2_out, C);
  and and_7 (O6, A, B, not_1_out);
  and and_8 (O7, A, B, C);
endmodule
