// Logisim project 3-to-8_Encoder_OR.circ as structural Verilog: 1 circuit, main circuit main
module main (
  input  I0,
  input  I1,
  input  I2,
  input  I3,
  input  I4,
  input  I5,
  input  I6,
  input  I7,
  output O1,
  output O2,
  output O3
);

  or or_1 (O1, I1, I3, I5, I7);
  or or_2 (O2, I2, I3, I6, I7);
  or or_3 (O3, I4, I5, I6, I7);
endmodule
