// Logisim project 4-to-1_MUX.circ as structural Verilog: 1 circuit, main circuit main
module main (
  input  I0,
  input  I1,
  input  I3,
  input  I4,
  input  [1:0] in_5,
  output Z
);

  Multiplexer #(.select(2), .enable("false")) multiplexer_1 (
    .in0(I0), .in1(I1), .in2(I3), .in3(I4), .out(Z), .sel(in_5));

  // Notes on the sheet:
  //   A     B     Z
  //   _________
  //   |
  //   |
  //   0     0     Input-0
  //   |
  //   0     1     Input-1
  //   |
  //   1     0     Input-2
  //   |
  //   |
  //   1     1     Input-3
  //   =
  //   __________
  //      A'B'I0+A'BI1+AB'I2+ABI3
endmodule
