// Logisim project 8-to-1_MUX.circ as structural Verilog: 1 circuit, main circuit main
module main (
  input  I0,
  input  I1,
  input  I3,
  input  I4,
  input  I5,
  input  I6,
  input  I7,
  input  [2:0] in_8,
  input  I8,
  output Z
);

  Multiplexer #(.select(3), .enable("false")) multiplexer_1 (
    .in0(I0), .in1(I1), .in2(I3), .in3(I4), .in4(I5), .in5(I6), .in6(I7), .in7(I8), .out(Z), .sel(in_8));

  // Notes on the sheet:
  //   A     B     C     Z
  //   =
  //   _________
  //   __________
  //   |
  //   |
  //   0      0      0     Input-0
  //   |
  //   0      0      1     Input-1
  //   |
  //   0      1      0     Input-2
  //   |
  //   0      1      1     Input-3
  //   |
  //   1      0      0     Input-4
  //   |
  //   1      0      1     Input-5
  //   |
  //   1      1      0     Input-6
  //   |
  //   1      1      1     Input-7
  //   |
  //   A'B'C'I0+A'B'C'I1+A'B'C'I2+A'B'C'I3+A'B'C'I4+A'B'C'I5+A'B'C'I6+A'B'C'I7
endmodule
