// Logisim project Multiple_4-to-1_MUX_Instead_8-to-1.circ as structural Verilog: 1 circuit, main circuit main
module main (
  input  I0,
  input  I1,
  input  I2,
  input  I3,
  input  I4,
  input  I5,
  input  I6,
  input  I7,
  input  I0_2,
  input  I1_2,
  input  I2_2,
  input  I3_2,
  input  I4_2,
  input  I5_2,
  input  I6_2,
  input  I7_2,
  input  I0_3,
  input  I1_3,
  input  I2_3,
  input  I3_3,
  input  I4_3,
  input  I5_3,
  input  I6_3,
  input  I7_3,
  input  I0_4,
  input  I1_4,
  input  I2_4,
  input  I3_4,
  input  I4_4,
  input  I5_4,
  input  I6_4,
  input  I7_4,
  input  [1:0] B_A,
  input  C,
  output out_35,
  output out_36,
  output out_37,
  output out_38
);

  wire multiplexer_1_out, multiplexer_2_out, multiplexer_3_out, multiplexer_4_out, multiplexer_5_out,
       multiplexer_6_out, multiplexer_7_out, multiplexer_8_out, not_1_out, not_2_out, not_3_out, not_4_out;

  Multiplexer #(.select(2), .disabled(0)) multiplexer_1 (
    .in0(I0), .in1(I1), .in2(I2), .in3(I3), .out(multiplexer_1_out), .sel(B_A), .en(not_1_out));
  Multiplexer #(.select(2), .disabled(0)) multiplexer_2 (
    .in0(I4), .in1(I5), .in2(I6), .in3(I7), .out(multiplexer_2_out), .sel(B_A), .en(C));
  Multiplexer #(.select(2), .disabled(0)) multiplexer_3 (
    .in0(I0_2), .in1(I1_2), .in2(I2_2), .in3(I3_2), .out(multiplexer_3_out), .sel(B_A), .en(not_2_out));
  Multiplexer #(.select(2), .disabled(0)) multiplexer_4 (
    .in0(I4_2), .in1(I5_2), .in2(I6_2), .in3(I7_2), .out(multiplexer_4_out), .sel(B_A), .en(C));
  Multiplexer #(.select(2), .disabled(0)) multiplexer_5 (
    .in0(I0_3), .in1(I1_3), .in2(I2_3), .in3(I3_3), .out(multiplexer_5_out), .sel(B_A), .en(not_3_out));
  Multiplexer #(.select(2), .disabled(0)) multiplexer_6 (
    .in0(I4_3), .in1(I5_3), .in2(I6_3), .in3(I7_3), .out(multiplexer_6_out), .sel(B_A), .en(C));
  Multiplexer #(.select(2), .disabled(0)) multiplexer_7 (
    .in0(I0_4), .in1(I1_4), .in2(I2_4), .in3(I3_4), .out(multiplexer_7_out), .sel(B_A), .en(not_4_out));
  Multiplexer #(.select(2), .disabled(0)) multiplexer_8 (
    .in0(I4_4), .in1(I5_4), .in2(I6_4), .in3(I7_4), .out(multiplexer_8_out), .sel(B_A), .en(C));
  not not_1 (not_1_out, C);
  not not_2 (not_2_out, C);
  not not_3 (not_3_out, C);
  not not_4 (not_4_out, C);
  or or_1 (out_35, multiplexer_1_out, multiplexer_2_out);
  or or_2 (out_36, multiplexer_3_out, multiplexer_4_out);
  or or_3 (out_37, multiplexer_5_out, multiplexer_6_out);
  or or_4 (out_38, multiplexer_7_out, multiplexer_8_out);
endmodule
