// Logisim project Multiple_8-to-1_MUX.circ as structural Verilog: 1 circuit, main circuit main
module main (
  input  I0,
  input  I1,
  input  I2,
  input  I3,
  input  I4,
  input  I5,
  input  I6,
  input  I7,
  input  I0_2,
  input  I1_2,
  input  I2_2,
  input  I3_2,
  input  I4_2,
  input  I5_2,
  input  I6_2,
  input  I7_2,
  input  I0_3,
  input  I1_3,
  input  I2_3,
  input  I3_3,
  input  I4_3,
  input  I5_3,
  input  I6_3,
  input  I7_3,
  input  I0_4,
  input  I1_4,
  input  I2_4,
  input  I3_4,
  input  I4_4,
  input  I5_4,
  input  I6_4,
  input  [2:0] in_32,
  input  I7_4,
  output Bit_0,
  output Bit_1,
  output Bit_2,
  output Bit_3
);

  Multiplexer #(.select(3), .enable("false")) multiplexer_1 (
    .in0(I0), .in1(I1), .in2(I2), .in3(I3), .in4(I4), .in5(I5), .in6(I6), .in7(I7), .out(Bit_0), .sel(in_32));
  Multiplexer #(.select(3), .enable("false")) multiplexer_2 (
    .in0(I0_2), .in1(I1_2), .in2(I2_2), .in3(I3_2), .in4(I4_2), .in5(I5_2), .in6(I6_2), .in7(I7_2),
    .out(Bit_1), .sel(in_32));
  Multiplexer #(.select(3), .enable("false")) multiplexer_3 (
    .in0(I0_3), .in1(I1_3), .in2(I2_3), .in3(I3_3), .in4(I4_3), .in5(I5_3), .in6(I6_3), .in7(I7_3),
    .out(Bit_2), .sel(in_32));
  Multiplexer #(.select(3), .enable("false")) multiplexer_4 (
    .in0(I0_4), .in1(I1_4), .in2(I2_4), .in3(I3_4), .in4(I4_4), .in5(I5_4), .in6(I6_4), .in7(I7_4),
    .out(Bit_3), .sel(in_32));
endmodule
