// Logisim project Flip_Flop(XAND).circ as structural Verilog: 1 circuit, main circuit main
module main (
  input  R_prime,
  input  S_prime,
  output Q,
  output Q_prime
);

  nand nand_1 (Q, R_prime, Q_prime);
  nand nand_2 (Q_prime, Q, S_prime);
endmodule
