// Logisim project Flip_Flops.circ as structural Verilog: 1 circuit, main circuit main
module main (
  input  D,
  input  G,
  input  D_2,
  input  G_2,
  input  D_3,
  input  G_3,
  output Q,
  output Q_prime,
  output Q_2,
  output Q_prime_2,
  output Q_3,
  output Q_prime_3
);

  wire and_1_out, and_2_out, and_3_out, and_4_out, and_5_out, and_6_out, clock_1_out, not_1_out, not_2_out,
       not_3_out, not_4_out, not_5_out;

  not not_1 (not_1_out, D);
  not not_2 (not_2_out, D_2);
  not not_3 (not_3_out, D_3);
  and and_1 (and_1_out, D, G);
  Clock clock_1 (.out(clock_1_out));
  and and_2 (and_2_out, G, not_1_out);
  and and_3 (and_3_out, D_2, G_2);
  and and_4 (and_4_out, G_2, not_2_out);
  and and_5 (and_5_out, D_3, G_3);
  and and_6 (and_6_out, G_3, not_3_out);
  S_R_Flip_Flop s_r_ff_1 (
    .S(and_1_out), .clk(clock_1_out), .R(and_2_out), .Q(Q), .Qn(Q_prime));  // open: preset, reset, en
  not not_4 (not_4_out, and_5_out);
  not not_5 (not_5_out, and_6_out);
  nor nor_1 (Q_2, and_3_out, Q_prime_2);
  nor nor_2 (Q_prime_2, Q_2, and_4_out);
  nand nand_1 (Q_3, not_4_out, Q_prime_3);
  nand nand_2 (Q_prime_3, Q_3, not_5_out);

  // Notes on the sheet:
  //   S
  //   R
  //   S
  //   R
endmodule
