// Logisim project T_Flip_Flop.circ as structural Verilog: 1 circuit, main circuit main
module main (
  input  T,
  output Q,
  output Q_prime
);

  wire clock_1_out;

  Clock clock_1 (.out(clock_1_out));
  T_Flip_Flop t_ff_1 (.clk(clock_1_out), .T(T), .Q(Q), .Qn(Q_prime));  // open: preset, reset, en
endmodule
