// Logisim project D-FF_with_MUX.circ as structural Verilog: 1 circuit, main circuit main
module main (
  input  D,
  input  CE,
  output out_3,
  output out_4
);

  wire clock_1_out, multiplexer_1_out;

  Clock clock_1 (.out(clock_1_out));
  Multiplexer multiplexer_1 (.in0(out_3), .in1(D), .out(multiplexer_1_out), .sel(CE));  // open: en
  D_Flip_Flop d_ff_1 (.clk(clock_1_out), .D(multiplexer_1_out), .Q(out_3), .Qn(out_4));  // open: preset, en, reset

  // Notes on the sheet:
  //   D Flip-Flop with MUX
endmodule
