// Logisim project D_to_T_Flip_Flop.circ as structural Verilog: 1 circuit, main circuit main
module main (
  input  in_1,
  output out_2,
  output out_3
);

  wire clock_1_out, xor_1_out;

  Clock clock_1 (.out(clock_1_out));
  xor xor_1 (xor_1_out, out_2, in_1);
  D_Flip_Flop d_ff_1 (.clk(clock_1_out), .D(xor_1_out), .Q(out_2), .Qn(out_3));  // open: preset, en, reset

  // Notes on the sheet:
  //   Morph D Flip-Flop into T Flip-Flop
endmodule
