// Logisim project JK_FF_to_T_FF.circ as structural Verilog: 1 circuit, main circuit main
module main (
  input  T,
  output out_2,
  output out_3
);

  wire clock_1_out;

  Clock clock_1 (.out(clock_1_out));
  J_K_Flip_Flop j_k_ff_1 (.J(T), .clk(clock_1_out), .K(T), .Q(out_2), .Qn(out_3));  // open: preset, en, reset

  // Notes on the sheet:
  //   JK Flip-Flop to T Flip-Flop
endmodule
