// Logisim project SR_Flip_Flop.circ as structural Verilog: 1 circuit, main circuit main
module main (
  input  S,
  input  R,
  output Q,
  output Q_prime
);

  wire and_1_out, and_2_out, and_3_out, and_4_out, Clock_out, not_1_out, s_r_ff_1_q, s_r_ff_1_qn;

  Clock Clock (.out(Clock_out));
  not not_1 (not_1_out, Clock_out);
  and and_1 (and_1_out, S, not_1_out);
  and and_2 (and_2_out, not_1_out, R);
  S_R_Flip_Flop s_r_ff_1 (
    .S(and_1_out), .R(and_2_out), .Q(s_r_ff_1_q), .Qn(s_r_ff_1_qn));  // open: clk, preset, reset, en
  and and_3 (and_3_out, s_r_ff_1_q, Clock_out);
  S_R_Flip_Flop s_r_ff_2 (.S(and_3_out), .R(and_4_out), .Q(Q), .Qn(Q_prime));  // open: clk, preset, reset, en
  and and_4 (and_4_out, s_r_ff_1_qn, Clock_out);

  // Notes on the sheet:
  //   SR Flip-Flop using SR Latch
endmodule
