// Logisim project S_R_to_J_K_Flip_Flop.circ as structural Verilog: 1 circuit, main circuit main
module main (
  input  J,
  input  K,
  output out_3,
  output out_4
);

  wire and_1_out, and_2_out, clock_1_out, not_1_out;

  and and_1 (and_1_out, out_4, not_1_out);
  not not_1 (not_1_out, J);
  and and_2 (and_2_out, out_3, K);
  S_R_Flip_Flop s_r_ff_1 (
    .S(and_1_out), .clk(clock_1_out), .R(and_2_out), .Q(out_3), .Qn(out_4));  // open: preset, reset, en
  Clock clock_1 (.out(clock_1_out));

  // Notes on the sheet:
  //   Morph S-R Flip-Flop into J-K Flip-Flop
endmodule
