// Logisim project 1bitBellekHucresi.circ as structural Verilog: 1 circuit, main circuit main
module main (
  input  Select,
  input  Input,
  input  Read_Write,
  output Output
);

  wire and_1_out, and_2_out, not_1_out, Output_out, s_r_ff_1_q;

  Clock u_Output (.out(Output_out));
  and and_1 (and_1_out, Select, Input, not_1_out);
  S_R_Flip_Flop s_r_ff_1 (
    .S(and_1_out), .clk(Output_out), .R(and_2_out), .Q(s_r_ff_1_q));  // open: Qn, preset, reset, en
  and and_2 (and_2_out, Select, ~Input, not_1_out);  // AND_Gate
  not not_1 (not_1_out, Read_Write);
  and and_3 (Output, Select, s_r_ff_1_q, Read_Write);
endmodule
