// Logisim project 4bitBinaryCounter.circ as structural Verilog: 1 circuit, main circuit main
module main (
  output Bit_1,
  output Bit_2,
  output Bit_3,
  output Bit_4,
  output out_5
);

  wire and_1_out, and_2_out, and_3_out, clock_1_out;

  and and_1 (and_1_out, 1'b1, Bit_1);
  and and_2 (and_2_out, and_1_out, Bit_2);
  and and_3 (and_3_out, and_2_out, Bit_3);
  Clock clock_1 (.out(clock_1_out));
  J_K_Flip_Flop j_k_ff_1 (.J(1'b1), .clk(clock_1_out), .K(1'b1), .Q(Bit_1));  // open: Qn, preset, en, reset
  J_K_Flip_Flop j_k_ff_2 (.J(and_1_out), .clk(clock_1_out), .K(and_1_out), .Q(Bit_2));  // open: Qn, preset, en, reset
  J_K_Flip_Flop j_k_ff_3 (.J(and_2_out), .clk(clock_1_out), .K(and_2_out), .Q(Bit_3));  // open: Qn, preset, en, reset
  J_K_Flip_Flop j_k_ff_4 (.J(and_3_out), .clk(clock_1_out), .K(and_3_out), .Q(Bit_4));  // open: Qn, preset, en, reset
  and and_4 (out_5, Bit_4, and_3_out);
endmodule
