// Logisim project 4bitBinaryCounterParallelLoad.circ as structural Verilog: 2 circuits, main circuit main
module main (
  input  Count,
  input  Load,
  input  Input0,
  input  Input1,
  input  Input2,
  input  Input3,
  input  Enabled,
  output [3:0] out_8,
  output Output0,
  output Output1,
  output Output2,
  output Output3,
  output Cout
);

  wire and_1_out, and_2_out, and_3_out, and_4_out, and_5_out, and_6_out, and_7_out, and_8_out, and_9_out,
       and_10_out, and_11_out, and_12_out, Clock_out, not_1_out, not_2_out, not_3_out, not_4_out, not_5_out,
       not_6_out, or_1_out, or_2_out, or_3_out, or_4_out, or_5_out, or_6_out, or_7_out, or_8_out;

  not not_1 (not_1_out, Load);
  Clock Clock (.out(Clock_out));
  and and_1 (and_1_out, Count, not_1_out);
  not not_2 (not_2_out, not_1_out);
  and and_2 (and_2_out, not_2_out, Input0);
  and and_3 (and_3_out, not_2_out, not_3_out);
  not not_3 (not_3_out, Input0);
  and and_4 (and_4_out, not_2_out, Input1);
  and and_5 (and_5_out, not_2_out, not_4_out);
  not not_4 (not_4_out, Input1);
  and and_6 (and_6_out, not_2_out, Input2);
  and and_7 (and_7_out, not_2_out, not_5_out);
  not not_5 (not_5_out, Input2);
  and and_8 (and_8_out, not_2_out, Input3);
  and and_9 (and_9_out, not_2_out, not_6_out);
  not not_6 (not_6_out, Input3);
  and and_10 (and_10_out, out_8[0], and_1_out);
  and and_11 (and_11_out, and_1_out, out_8[0], out_8[1]);
  and and_12 (and_12_out, out_8[2], out_8[1], out_8[0], and_1_out);
  or or_1 (or_1_out, and_1_out, and_2_out);
  or or_2 (or_2_out, and_1_out, and_3_out);
  or or_3 (or_3_out, and_10_out, and_4_out);
  or or_4 (or_4_out, and_10_out, and_5_out);
  or or_5 (or_5_out, and_11_out, and_6_out);
  or or_6 (or_6_out, and_11_out, and_7_out);
  or or_7 (or_7_out, and_12_out, and_8_out);
  or or_8 (or_8_out, and_12_out, and_9_out);
  J_K_Flip_Flop j_k_ff_1 (
    .J(or_1_out), .clk(Clock_out), .K(or_2_out), .Q(out_8[0]), .en(Enabled));  // open: Qn, preset, reset
  J_K_Flip_Flop j_k_ff_2 (
    .J(or_3_out), .clk(Clock_out), .K(or_4_out), .Q(out_8[1]), .en(Enabled));  // open: Qn, preset, reset
  J_K_Flip_Flop j_k_ff_3 (
    .J(or_5_out), .clk(Clock_out), .K(or_6_out), .Q(out_8[2]), .en(Enabled));  // open: Qn, preset, reset
  J_K_Flip_Flop j_k_ff_4 (
    .J(or_7_out), .clk(Clock_out), .K(or_8_out), .Q(out_8[3]), .en(Enabled));  // open: Qn, preset, reset
  and and_13 (Cout, out_8[3], out_8[2], out_8[1], out_8[0], and_1_out);

  assign Output0 = out_8[0];
  assign Output1 = out_8[1];
  assign Output2 = out_8[2];
  assign Output3 = out_8[3];
endmodule

module Birim_Devre (
  input  Count,
  input  Load,
  input  Input0,
  output Output0
);

  wire and_1_out, and_2_out, and_3_out, clock_1_out, not_1_out, not_2_out, not_3_out, or_1_out, or_2_out;

  not not_1 (not_1_out, Load);
  and and_1 (and_1_out, Count, not_1_out);
  not not_2 (not_2_out, not_1_out);
  and and_2 (and_2_out, not_2_out, Input0);
  and and_3 (and_3_out, not_2_out, not_3_out);
  not not_3 (not_3_out, Input0);
  or or_1 (or_1_out, and_1_out, and_2_out);
  Clock clock_1 (.out(clock_1_out));
  or or_2 (or_2_out, and_1_out, and_3_out);
  J_K_Flip_Flop j_k_ff_1 (
    .J(or_1_out), .clk(clock_1_out), .K(or_2_out), .Q(Output0), .en(1'b1));  // open: Qn, preset, reset
endmodule
