// Logisim project 4bitUpDownBinaryCounter.circ as structural Verilog: 1 circuit, main circuit main
module main (
  input  Up,
  input  Down,
  output Bit_1,
  output Bit_2,
  output Bit_3,
  output Bit_4
);

  wire and_1_out, and_2_out, and_3_out, and_4_out, and_5_out, and_6_out, and_7_out, clock_1_out, or_1_out,
       or_2_out, or_3_out, or_4_out, t_ff_1_qn, t_ff_2_qn, t_ff_3_qn;

  and and_1 (and_1_out, ~Up, Down);  // AND_Gate
  or or_1 (or_1_out, Up, and_1_out);
  and and_2 (and_2_out, and_1_out, t_ff_1_qn);
  and and_3 (and_3_out, Up, Bit_1);
  and and_4 (and_4_out, and_2_out, t_ff_2_qn);
  and and_5 (and_5_out, and_3_out, Bit_2);
  and and_6 (and_6_out, and_5_out, Bit_3);
  and and_7 (and_7_out, and_4_out, t_ff_3_qn);
  or or_2 (or_2_out, and_3_out, and_2_out);
  or or_3 (or_3_out, and_5_out, and_4_out);
  or or_4 (or_4_out, and_6_out, and_7_out);
  Clock clock_1 (.out(clock_1_out));
  T_Flip_Flop t_ff_1 (.clk(clock_1_out), .T(or_1_out), .Q(Bit_1), .Qn(t_ff_1_qn));  // open: preset, reset, en
  T_Flip_Flop t_ff_2 (.clk(clock_1_out), .T(or_2_out), .Q(Bit_2), .Qn(t_ff_2_qn));  // open: preset, reset, en
  T_Flip_Flop t_ff_3 (.clk(clock_1_out), .T(or_3_out), .Q(Bit_3), .Qn(t_ff_3_qn));  // open: preset, reset, en
  T_Flip_Flop t_ff_4 (.clk(clock_1_out), .T(or_4_out), .Q(Bit_4));  // open: Qn, preset, reset, en
endmodule
