// Logisim project DataTransferBetweenRegisters.circ as structural Verilog: 3 circuits, main circuit main
module main (
  input  in_1,
  input  in_2
);

  wire clock_1_out, control_1_q1, control_1_q2, control_1_q3;
  wire [3:0] controlled_buffer_1_out, R1_output, R2_output, R3_output;

  Clock clock_1 (.out(clock_1_out));
  control control_1 (.C1(in_1), .C2(in_2), .Q1(control_1_q1), .Q2(control_1_q2), .Q3(control_1_q3));
  // Probe on R1_output
  register R1 (
    .Input(controlled_buffer_1_out), .Clock(clock_1_out), .Load(control_1_q1), .Output(R1_output));  // open: Increment, Clear
  // Probe on R2_output
  register R2 (
    .Input(controlled_buffer_1_out), .Clock(clock_1_out), .Load(control_1_q2), .Output(R2_output));  // open: Increment, Clear
  // Probe on R3_output
  register R3 (
    .Input(controlled_buffer_1_out), .Clock(clock_1_out), .Load(control_1_q3), .Output(R3_output));  // open: Increment, Clear
  assign controlled_buffer_1_out = control_1_q3 ? R1_output : 4'bz;  // Controlled_Buffer controlled_buffer_1
  assign controlled_buffer_1_out = control_1_q1 ? R2_output : 4'bz;  // Controlled_Buffer controlled_buffer_2
  assign controlled_buffer_1_out = control_1_q2 ? R3_output : 4'bz;  // Controlled_Buffer controlled_buffer_3
  // Probe on controlled_buffer_1_out
endmodule

// reg
module register (
  input  Increment,
  input  Load,
  input  [3:0] Input,
  input  Clock,
  input  Clear,
  output [3:0] Output
);

  wire and_1_out, and_2_out, and_3_out, and_4_out, and_5_out, and_6_out, and_7_out, and_8_out, and_9_out,
       and_10_out, and_11_out, and_12_out, not_1_out, not_2_out, or_1_out, or_2_out, or_3_out, or_4_out,
       or_5_out, or_6_out, or_7_out, or_8_out;

  not not_1 (not_1_out, Load);
  and and_1 (and_1_out, Increment, not_1_out);
  not not_2 (not_2_out, not_1_out);
  and and_2 (and_2_out, not_2_out, Input[0]);
  and and_3 (and_3_out, not_2_out, ~Input[0]);  // AND_Gate
  and and_4 (and_4_out, not_2_out, Input[1]);
  and and_5 (and_5_out, not_2_out, ~Input[1]);  // AND_Gate
  and and_6 (and_6_out, not_2_out, Input[2]);
  and and_7 (and_7_out, not_2_out, ~Input[2]);  // AND_Gate
  and and_8 (and_8_out, not_2_out, Input[3]);
  and and_9 (and_9_out, not_2_out, ~Input[3]);  // AND_Gate
  and and_10 (and_10_out, Output[0], and_1_out);
  and and_11 (and_11_out, Output[1], Output[0], and_1_out);
  and and_12 (and_12_out, Output[2], Output[1], Output[0], and_1_out);
  or or_1 (or_1_out, and_1_out, and_2_out);
  J_K_Flip_Flop j_k_ff_1 (
    .J(or_1_out), .clk(Clock), .K(or_2_out), .Q(Output[0]), .reset(Clear));  // open: Qn, preset, en
  or or_2 (or_2_out, and_1_out, and_3_out);
  or or_3 (or_3_out, and_4_out, and_10_out);
  J_K_Flip_Flop j_k_ff_2 (
    .J(or_3_out), .clk(Clock), .K(or_4_out), .Q(Output[1]), .reset(Clear));  // open: Qn, preset, en
  or or_4 (or_4_out, and_10_out, and_5_out);
  or or_5 (or_5_out, and_6_out, and_11_out);
  J_K_Flip_Flop j_k_ff_3 (
    .J(or_5_out), .clk(Clock), .K(or_6_out), .Q(Output[2]), .reset(Clear));  // open: Qn, preset, en
  or or_6 (or_6_out, and_11_out, and_7_out);
  or or_7 (or_7_out, and_8_out, and_12_out);
  J_K_Flip_Flop j_k_ff_4 (
    .J(or_7_out), .clk(Clock), .K(or_8_out), .Q(Output[3]), .reset(Clear));  // open: Qn, preset, en
  or or_8 (or_8_out, and_12_out, and_9_out);
endmodule

module control (
  input  C1,
  input  C2,
  output Q1,
  output Q2,
  output Q3
);

  wire not_1_out, not_2_out;

  not not_1 (not_1_out, C1);
  not not_2 (not_2_out, C2);
  and and_1 (Q1, not_1_out, not_2_out);
  and and_2 (Q2, not_1_out, C2);
  and and_3 (Q3, C1, not_2_out);
endmodule
