// Logisim project genel.circ as structural Verilog
module main (
  input  in_1,
  input  in_2
);

  wire clock_1_out, control_1_q1, control_1_q2, control_1_q3;
  wire [3:0] controlled_buffer_1_out, R1_output, R2_output, R3_output;

  Clock clock_1 (.out(clock_1_out));
  control control_1 (.C1(in_1), .C2(in_2), .Q1(control_1_q1), .Q2(control_1_q2), .Q3(control_1_q3));
  // Probe on R1_output
  _4_REG R1 (
    .Input(controlled_buffer_1_out), .Clock(clock_1_out), .Load(control_1_q1), .Output(R1_output));  // open: Increment, Clear
  // Probe on R2_output
  _4_REG R2 (
    .Input(controlled_buffer_1_out), .Clock(clock_1_out), .Load(control_1_q2), .Output(R2_output));  // open: Increment, Clear
  // Probe on R3_output
  _4_REG R3 (
    .Input(controlled_buffer_1_out), .Clock(clock_1_out), .Load(control_1_q3), .Output(R3_output));  // open: Increment, Clear
  assign controlled_buffer_1_out = control_1_q3 ? R1_output : 4'bz;  // Controlled_Buffer controlled_buffer_1
  assign controlled_buffer_1_out = control_1_q1 ? R2_output : 4'bz;  // Controlled_Buffer controlled_buffer_2
  assign controlled_buffer_1_out = control_1_q2 ? R3_output : 4'bz;  // Controlled_Buffer controlled_buffer_3
  // Probe on controlled_buffer_1_out
endmodule

module control (
  input  C1,
  input  C2,
  output Q1,
  output Q2,
  output Q3
);

  wire not_1_out, not_2_out;

  not not_1 (not_1_out, C1);
  not not_2 (not_2_out, C2);
  and and_1 (Q1, not_1_out, not_2_out);
  and and_2 (Q2, not_1_out, C2);
  and and_3 (Q3, C1, not_2_out);
endmodule

module devre (
  input  [3:0] INPR,
  output E
);

  wire CLK_out, undriven, undriven_2, undriven_3, undriven_4, undriven_5, undriven_6, undriven_7;
  wire [3:0] AC_output, alu_cu4_1_output__ac, AR_output, DR_output, OUTR_output, PC_output;
  wire [7:0] controlled_buffer_1_out, IR_output, ram_1_data;

  Clock CLK (.out(CLK_out));
  ALU_CU4 alu_cu4_1 (
    .AC(AC_output), .DR(DR_output), .INPR(INPR), .AND(undriven), .ADD(undriven_2), .LD_RD(undriven_3),
    .COMP(undriven_4), .LD_INPR(undriven_5), .CIR(undriven_6), .CIL(undriven_7), .E_AC_0(E),
    .Output__AC(alu_cu4_1_output__ac));  // open: Cin, Cout
  // Probe on AR_output
  _4_REG AR (
    .Input(controlled_buffer_1_out[3:0]), .Clock(CLK_out), .Output(AR_output));  // open: Load, Increment, Clear
  // Probe on PC_output
  _4_REG PC (
    .Input(controlled_buffer_1_out[3:0]), .Clock(CLK_out), .Output(PC_output));  // open: Load, Increment, Clear
  // Probe on DR_output
  _4_REG DR (
    .Input(controlled_buffer_1_out[3:0]), .Clock(CLK_out), .Output(DR_output));  // open: Load, Increment, Clear
  _4_REG AC (.Input(alu_cu4_1_output__ac), .Clock(CLK_out), .Output(AC_output));  // open: Load, Increment, Clear
  _8_REG IR (.INPUT(controlled_buffer_1_out), .CLK(CLK_out), .OUTPUT(IR_output));  // open: LD, INC, CLR
  _4_REG OUTR (
    .Input(controlled_buffer_1_out[3:0]), .Clock(CLK_out), .Output(OUTR_output));  // open: Load, Increment, Clear
  // Probe on OUTR_output
  Controlled_Buffer #(.width(8)) controlled_buffer_1 (.in(ram_1_data), .out(controlled_buffer_1_out));  // open: en
  RAM #(.addrWidth(4), .bus("separate")) ram_1 (
    .addr(AR_output), .din(controlled_buffer_1_out), .data(ram_1_data), .clk(CLK_out));  // open: str, sel, ld, clr
  Controlled_Buffer #(.width(8)) controlled_buffer_2 (
    .in({4'b0000, AR_output}), .out(controlled_buffer_1_out));  // open: en
  Controlled_Buffer #(.width(8)) controlled_buffer_3 (
    .in({4'b0000, PC_output}), .out(controlled_buffer_1_out));  // open: en
  Controlled_Buffer #(.width(8)) controlled_buffer_4 (
    .in({4'b0000, DR_output}), .out(controlled_buffer_1_out));  // open: en
  // Probe on AC_output
  Controlled_Buffer #(.width(8)) controlled_buffer_5 (
    .in({4'b0000, AC_output}), .out(controlled_buffer_1_out));  // open: en
  // Probe on IR_output
  Controlled_Buffer #(.width(8)) controlled_buffer_6 (.in(IR_output), .out(controlled_buffer_1_out));  // open: en
endmodule

// reg
module _4_REG (
  input  Increment,
  input  Load,
  input  [3:0] Input,
  input  Clock,
  input  Clear,
  output [3:0] Output
);

  wire and_1_out, and_2_out, and_3_out, and_4_out, and_5_out, and_6_out, and_7_out, and_8_out, and_9_out,
       and_10_out, and_11_out, and_12_out, not_1_out, not_2_out, or_1_out, or_2_out, or_3_out, or_4_out,
       or_5_out, or_6_out, or_7_out, or_8_out;

  not not_1 (not_1_out, Load);
  and and_1 (and_1_out, Increment, not_1_out);
  not not_2 (not_2_out, not_1_out);
  and and_2 (and_2_out, not_2_out, Input[0]);
  and and_3 (and_3_out, not_2_out, ~Input[0]);  // AND_Gate
  and and_4 (and_4_out, not_2_out, Input[1]);
  and and_5 (and_5_out, not_2_out, ~Input[1]);  // AND_Gate
  and and_6 (and_6_out, not_2_out, Input[2]);
  and and_7 (and_7_out, not_2_out, ~Input[2]);  // AND_Gate
  and and_8 (and_8_out, not_2_out, Input[3]);
  and and_9 (and_9_out, not_2_out, ~Input[3]);  // AND_Gate
  and and_10 (and_10_out, Output[0], and_1_out);
  and and_11 (and_11_out, Output[1], Output[0], and_1_out);
  and and_12 (and_12_out, Output[2], Output[1], Output[0], and_1_out);
  or or_1 (or_1_out, and_1_out, and_2_out);
  J_K_Flip_Flop j_k_ff_1 (
    .J(or_1_out), .clk(Clock), .K(or_2_out), .Q(Output[0]), .reset(Clear));  // open: Qn, preset, en
  or or_2 (or_2_out, and_1_out, and_3_out);
  or or_3 (or_3_out, and_4_out, and_10_out);
  J_K_Flip_Flop j_k_ff_2 (
    .J(or_3_out), .clk(Clock), .K(or_4_out), .Q(Output[1]), .reset(Clear));  // open: Qn, preset, en
  or or_4 (or_4_out, and_10_out, and_5_out);
  or or_5 (or_5_out, and_6_out, and_11_out);
  J_K_Flip_Flop j_k_ff_3 (
    .J(or_5_out), .clk(Clock), .K(or_6_out), .Q(Output[2]), .reset(Clear));  // open: Qn, preset, en
  or or_6 (or_6_out, and_11_out, and_7_out);
  or or_7 (or_7_out, and_8_out, and_12_out);
  J_K_Flip_Flop j_k_ff_4 (
    .J(or_7_out), .clk(Clock), .K(or_8_out), .Q(Output[3]), .reset(Clear));  // open: Qn, preset, en
  or or_8 (or_8_out, and_12_out, and_9_out);
endmodule

module _8_REG (
  input  [7:0] INPUT,
  input  CLK,
  input  LD,
  input  INC,
  input  CLR,
  output [7:0] OUTPUT
);

  // Probe on INPUT
  _4_REG u_4_reg_1 (.Input(INPUT[3:0]), .Clock(CLK), .Load(LD), .Increment(INC), .Clear(CLR), .Output(OUTPUT[3:0]));
  _4_REG u_4_reg_2 (.Input(INPUT[7:4]), .Clock(CLK), .Load(LD), .Increment(INC), .Clear(CLR), .Output(OUTPUT[7:4]));
endmodule

module noname (
  input  [3:0] INPR,
  output [3:0] out_2
);

  wire ar_control_1_ar_bus, ar_control_1_ar_inc, ar_control_1_ar_ld, CLK_out;
  wire [3:0] AC_output, AR_output, controlled_buffer_1_out, controlled_buffer_1_out_2, DR_output, PC_output;
  wire [7:0] IR_output, ram_1_data;

  AR_Control ar_control_1 (
    .AR_LD(ar_control_1_ar_ld), .AR_INC(ar_control_1_ar_inc), .AR_BUS(ar_control_1_ar_bus));  // open: TO, T2, T3, T4, D4, D5
  Clock CLK (.out(CLK_out));
  // Probe on AR_output
  _4_REG AR (
    .Input(controlled_buffer_1_out), .Clock(CLK_out), .Load(ar_control_1_ar_ld),
    .Increment(ar_control_1_ar_inc), .Output(AR_output));  // open: Clear
  // Probe on PC_output
  _4_REG PC (.Input(controlled_buffer_1_out), .Clock(CLK_out), .Output(PC_output));  // open: Load, Increment, Clear
  // Probe on DR_output
  _4_REG DR (.Input(controlled_buffer_1_out), .Clock(CLK_out), .Output(DR_output));  // open: Load, Increment, Clear
  _4_REG AC (.Clock(CLK_out), .Output(AC_output));  // open: Input, Load, Increment, Clear
  _8_REG IR (
    .INPUT({controlled_buffer_1_out_2, controlled_buffer_1_out}), .CLK(CLK_out), .OUTPUT(IR_output));  // open: LD, INC, CLR
  _4_REG OUTR (.Input(controlled_buffer_1_out), .Clock(CLK_out), .Output(out_2));  // open: Load, Increment, Clear
  Controlled_Buffer #(.width(8)) controlled_buffer_1 (
    .in(ram_1_data), .out({controlled_buffer_1_out_2, controlled_buffer_1_out}));  // open: en
  RAM #(.addrWidth(4), .bus("separate")) ram_1 (
    .addr(AR_output), .din({controlled_buffer_1_out_2, controlled_buffer_1_out}), .data(ram_1_data),
    .clk(CLK_out));  // open: str, sel, ld, clr
  assign {controlled_buffer_1_out_2, controlled_buffer_1_out} = ar_control_1_ar_bus ? {4'b0000, AR_output} : 8'bz;  // Controlled_Buffer controlled_buffer_2
  Controlled_Buffer #(.width(8)) controlled_buffer_3 (
    .in({4'b0000, PC_output}), .out({controlled_buffer_1_out_2, controlled_buffer_1_out}));  // open: en
  Controlled_Buffer #(.width(8)) controlled_buffer_4 (
    .in({4'b0000, DR_output}), .out({controlled_buffer_1_out_2, controlled_buffer_1_out}));  // open: en
  // Probe on AC_output
  Controlled_Buffer #(.width(8)) controlled_buffer_5 (
    .in({4'b0000, AC_output}), .out({controlled_buffer_1_out_2, controlled_buffer_1_out}));  // open: en
  // Probe on IR_output
  Controlled_Buffer #(.width(8)) controlled_buffer_6 (
    .in(IR_output), .out({controlled_buffer_1_out_2, controlled_buffer_1_out}));  // open: en
  // Probe on {controlled_buffer_1_out_2, controlled_buffer_1_out}

  // Notes on the sheet:
  //   Ar ld Ar ld girişine
  //   main control buraya eklenir
  //   splitter ile ar'nin 4-7 arası alınacak
  //   memory load str ucuna
  //   memory bus D çıkışındaki buffera
  //   bus olanlar genel olarak bufferlara
  //   alu buraya
  //   counter doğrudan kullanıldığında bi sıkıntı oluyormuş, ondan counter'ı manuel geliştirmemizi istemiş
  //   gönüllü olarak bitirenler getirip gösterebilir dedi
endmodule

// AR Control
module AR_Control (
  input  TO,
  input  T2,
  input  T3,
  input  T4,
  input  D4,
  input  D5,
  output AR_LD,
  output AR_INC,
  output AR_BUS
);

  wire and_2_out, and_3_out;

  or or_1 (AR_LD, T2, TO);
  and and_1 (AR_INC, T3, D5);
  and and_2 (and_2_out, D4, T3);
  and and_3 (and_3_out, D5, T4);
  or or_2 (AR_BUS, and_2_out, and_3_out);

  // Notes on the sheet:
  //   AR içeren komutları topladı, bir araya getirdikten sonra aynı işlemi yapanları ayırdı.
endmodule

module main_control_unit (
  input  [3:0] IR_4_7,
  input  sc
);

  wire [3:0] undriven;

  Decoder #(.select(4)) decoder_1 (.sel(IR_4_7));  // open: out0, out1, out2, out3, out4, out5, out6, out7, out8, out9, out10, out11, out12, out13, out14, out15, en
  Decoder #(.select(4)) decoder_2 (.sel(undriven));  // open: out0, out1, out2, out3, out4, out5, out6, out7, out8, out9, out10, out11, out12, out13, out14, out15, en

  // Notes on the sheet:
  //   D0_D15
  //   1 tane sc alt'a giriyor
  //   sc_clear
  //   (foto aldım)
  //   T0_T4
  //   memory
  //   AR
  //   PC
  //   -
  //   araya controllerları dizdi, çıktılara göre decoderlerin çıktılarını onlara aktaracak
  //   ALU
  //   son hali fotoda
endmodule

module ALU (
  input  S3,
  input  S2,
  input  in_3,
  input  S1,
  input  S0,
  input  Bi,
  input  Ai,
  input  Ai_1,
  input  Ai_1_2,
  output F
);

  wire aritmetic_circuit_1_d0, logic_circuit_1_fi;

  aritmetic_circuit aritmetic_circuit_1 (.Cin(in_3), .S0(S1), .S1(S0), .A0(Bi), .B0(Ai), .D0(aritmetic_circuit_1_d0));
  logic_circuit logic_circuit_1 (.Ai(S1), .Bi(S0), .S0(Bi), .S1(Ai), .Fi(logic_circuit_1_fi));
  Multiplexer #(.select(2)) multiplexer_1 (
    .in0(aritmetic_circuit_1_d0), .in1(logic_circuit_1_fi), .in2(Ai_1), .in3(Ai_1_2), .out(F), .sel({S2, S3}));  // open: en
endmodule

module ALU_CU1 (
  input  INPR,
  input  DR,
  input  AC,
  input  AND,
  input  Cin,
  input  ADD,
  input  Id_INPR,
  input  COMP,
  input  Id_DR,
  input  SHR,
  input  SHL,
  input  AC_i_1,
  input  AC_i_1_2,
  output Cout,
  output Output__AC
);

  wire adder_1_out, and_1_out, and_2_out, and_3_out, and_4_out, and_5_out, and_6_out, and_7_out, and_8_out,
       not_1_out;

  Adder #(.width(1)) adder_1 (.a(AC), .b(DR), .out(adder_1_out), .cin(Cin), .cout(Cout));
  and and_1 (and_1_out, AND, and_2_out);
  and and_2 (and_2_out, AC, DR);
  and and_3 (and_3_out, ADD, adder_1_out);
  and and_4 (and_4_out, Id_INPR, DR);
  and and_5 (and_5_out, COMP, not_1_out);
  not not_1 (not_1_out, AC);
  and and_6 (and_6_out, Id_DR, INPR);
  and and_7 (and_7_out, SHR, AC_i_1_2);
  and and_8 (and_8_out, SHL, AC_i_1);
  or or_1 (Output__AC, and_1_out, and_3_out, and_4_out, and_5_out, and_6_out, and_7_out, and_8_out);
endmodule

module ALU_CU4 (
  input  E_AC_0,
  input  Cin,
  input  [3:0] AC,
  input  [3:0] DR,
  input  [3:0] INPR,
  input  AND,
  input  ADD,
  input  LD_RD,
  input  COMP,
  input  LD_INPR,
  input  CIR,
  input  CIL,
  output [3:0] Output__AC,
  output Cout
);

  wire alu_cu1_1_cout, alu_cu1_2_cout, alu_cu1_3_cout;

  ALU_CU1 alu_cu1_1 (
    .AND(AND), .ADD(ADD), .Id_INPR(LD_RD), .COMP(COMP), .Id_DR(LD_INPR), .SHR(CIR), .SHL(CIL),
    .AC_i_1(E_AC_0), .AC_i_1_2(AC[1]), .INPR(INPR[0]), .DR(DR[0]), .AC(AC[0]), .Cin(Cin),
    .Cout(alu_cu1_1_cout), .Output__AC(Output__AC[0]));
  ALU_CU1 alu_cu1_2 (
    .AND(AND), .ADD(ADD), .Id_INPR(LD_RD), .COMP(COMP), .Id_DR(LD_INPR), .SHR(CIR), .SHL(CIL),
    .AC_i_1(AC[0]), .AC_i_1_2(AC[2]), .INPR(INPR[1]), .DR(DR[1]), .AC(AC[1]), .Cin(alu_cu1_1_cout),
    .Cout(alu_cu1_2_cout), .Output__AC(Output__AC[1]));
  ALU_CU1 alu_cu1_3 (
    .AND(AND), .ADD(ADD), .Id_INPR(LD_RD), .COMP(COMP), .Id_DR(LD_INPR), .SHR(CIR), .SHL(CIL),
    .AC_i_1(AC[1]), .AC_i_1_2(AC[3]), .INPR(INPR[2]), .DR(DR[2]), .AC(AC[2]), .Cin(alu_cu1_2_cout),
    .Cout(alu_cu1_3_cout), .Output__AC(Output__AC[2]));
  ALU_CU1 alu_cu1_4 (
    .AND(AND), .ADD(ADD), .Id_INPR(LD_RD), .COMP(COMP), .Id_DR(LD_INPR), .SHR(CIR), .SHL(CIL),
    .AC_i_1(AC[2]), .INPR(INPR[3]), .DR(DR[3]), .AC(AC[3]), .Cin(alu_cu1_3_cout), .Cout(Cout),
    .Output__AC(Output__AC[3]));  // open: AC_i_1_2
endmodule

// Aritmetic
module aritmetic_circuit (
  input  Cin,
  input  S0,
  input  S1,
  input  A0,
  input  B0,
  output D0
);

  wire multiplexer_1_out, not_1_out, not_2_out;

  not not_1 (not_1_out, B0);
  not not_2 (not_2_out, 1'b0);
  Multiplexer #(.select(2)) multiplexer_1 (
    .in0(B0), .in1(not_1_out), .in2(1'b0), .in3(not_2_out), .out(multiplexer_1_out), .sel({S1, S0}));  // open: en
  Adder #(.width(1)) adder_1 (.a(A0), .b(multiplexer_1_out), .out(D0), .cin(Cin));  // open: cout
endmodule

// Logic
module logic_circuit (
  input  Ai,
  input  Bi,
  input  S0,
  input  S1,
  output Fi
);

  wire and_1_out, not_1_out, or_1_out, xor_1_out;

  and and_1 (and_1_out, Ai, Bi);
  or or_1 (or_1_out, Ai, Bi);
  xor xor_1 (xor_1_out, Ai, Bi);
  not not_1 (not_1_out, Bi);
  Multiplexer #(.select(2)) multiplexer_1 (
    .in0(and_1_out), .in1(or_1_out), .in2(xor_1_out), .in3(not_1_out), .out(Fi), .sel({S1, S0}));  // open: en
endmodule
