// Logisim project Lab1Q1.circ as structural Verilog: 1 circuit, main circuit main
module main (
  input  A,
  input  B,
  input  C,
  input  A_2,
  input  B_2,
  input  C_2,
  input  A_3,
  input  B_3,
  input  C_3,
  output out_10,
  output out_11,
  output out_12
);

  wire and_1_out, and_2_out, and_3_out, and_4_out, and_5_out, and_6_out, and_7_out, and_8_out, and_9_out,
       and_10_out, and_11_out, not_1_out, not_2_out, not_3_out, or_1_out, or_3_out, or_4_out, or_5_out;

  and and_1 (and_1_out, B_3, C_3);
  not not_1 (not_1_out, and_2_out);
  and and_2 (and_2_out, A, B);
  and and_3 (and_3_out, A, C);
  and and_4 (and_4_out, ~B, C);  // AND_Gate
  and and_5 (and_5_out, A_2, B_2, ~C_2);  // AND_Gate
  and and_6 (and_6_out, ~A_2, B_2, C_2);  // AND_Gate
  and and_7 (and_7_out, A_2, ~B_2);  // AND_Gate
  and and_8 (and_8_out, ~A_2, B_2);  // AND_Gate
  or or_1 (or_1_out, ~A_3, B_3);  // OR_Gate
  and and_9 (and_9_out, B_3, ~C_3);  // AND_Gate
  not not_2 (not_2_out, and_1_out);
  or or_2 (out_10, not_1_out, and_3_out, and_4_out);
  or or_3 (or_3_out, and_5_out, and_6_out);
  or or_4 (or_4_out, and_7_out, and_8_out);
  or or_5 (or_5_out, B_3, ~and_9_out);  // OR_Gate
  and and_10 (and_10_out, A_3, not_2_out);
  not not_3 (not_3_out, or_3_out);
  and and_11 (and_11_out, or_1_out, or_5_out);
  and and_12 (out_11, not_3_out, or_4_out);
  or or_6 (out_12, and_11_out, and_10_out);

  // Notes on the sheet:
  //   F1
  //   F2
  //   F3
endmodule
