// Logisim project Lab1Q2.circ as structural Verilog: 1 circuit, main circuit main
module main (
  input  A,
  input  B,
  input  C,
  input  A_2,
  input  B_2,
  input  C_2,
  output out_7,
  output out_8
);

  wire and_1_out, and_2_out, and_3_out, and_4_out, and_5_out, and_6_out, nand_1_out, nand_2_out, not_1_out,
       not_2_out, or_1_out, or_2_out, xor_1_out;

  not not_1 (not_1_out, A);
  nand nand_1 (nand_1_out, B, A);
  or or_1 (or_1_out, nand_1_out, C);
  not not_2 (not_2_out, A_2);
  nand nand_2 (nand_2_out, B_2, C_2);
  or or_2 (or_2_out, nand_2_out, A_2);
  and and_1 (and_1_out, nand_2_out, C_2);
  and and_2 (and_2_out, C_2, B_2);
  and and_3 (and_3_out, not_1_out, C);
  and and_4 (and_4_out, not_1_out, or_1_out);
  and and_5 (and_5_out, not_2_out, B_2);
  and and_6 (and_6_out, not_2_out, or_2_out);
  xor xor_1 (xor_1_out, and_1_out, and_2_out);
  xor xor_2 (out_7, and_3_out, and_4_out);
  or or_3 (out_8, and_5_out, and_6_out, xor_1_out);

  // Notes on the sheet:
  //   F1
  //   F2
endmodule
