// Logisim project Lab2.circ as structural Verilog: 2 circuits, main circuit main
module main (
  input  CLK,
  output Q3,
  output Q2,
  output Q1,
  output Q0
);

  wire nand_1_out;

  _2bit_sayici a (.CLK(nand_1_out), .Q1(Q3), .Q0(Q2));
  _2bit_sayici b (.CLK(CLK), .Q1(Q1), .Q0(Q0));
  nand nand_1 (nand_1_out, Q1, Q0);
endmodule

module _2bit_sayici (
  input  CLK,
  output Q1,
  output Q0
);

  J_K_Flip_Flop j_k_ff_1 (.J(Q0), .clk(CLK), .K(Q0), .Q(Q1));  // open: Qn, preset, en, reset
  J_K_Flip_Flop j_k_ff_2 (.J(1'b1), .clk(CLK), .K(1'b1), .Q(Q0));  // open: Qn, preset, en, reset
endmodule
